# Fritzing sketch analog_board (saved by Fritzing 0.9.0b)
circuit board: 14.439cm x 7.49893cm
breadboards: 1

parts:
  IC1 = CD22M3494 [package=THT]
  IC2 = AD8403 [package=TSSOP]
  IN0 = female pin header, 2 pins [form="♀ (female)"]
  IN1 = female pin header, 2 pins [form="♀ (female)"]
  IC3 = AD8403 [package=TSSOP]
  IN2 = female pin header, 2 pins [form="♀ (female)"]
  IN3 = female pin header, 2 pins [form="♀ (female)"]
  IC5 = AD8403 [package=TSSOP]
  IC4 = AD8403 [package=TSSOP]
  IN4 = female pin header, 2 pins [form="♀ (female)"]
  IN5 = female pin header, 2 pins [form="♀ (female)"]
  IN6 = female pin header, 2 pins [form="♀ (female)"]
  IN7 = female pin header, 2 pins [form="♀ (female)"]
  IC6 = CD22M3494 [package=THT]
  OUT4 = female pin header, 2 pins [form="♀ (female)"]
  OUT5 = female pin header, 2 pins [form="♀ (female)"]
  OUT6 = female pin header, 2 pins [form="♀ (female)"]
  OUT7 = female pin header, 2 pins [form="♀ (female)"]
  OUT2 = female pin header, 2 pins [form="♀ (female)"]
  OUT1 = female pin header, 2 pins [form="♀ (female)"]
  OUT0 = female pin header, 2 pins [form="♀ (female)"]
  OUT3 = female pin header, 2 pins [form="♀ (female)"]
  CTRL1 = female pin header, 2 pins [form="♀ (female)"]
  CTRL2 = female pin header, 2 pins [form="♀ (female)"]
  CTRL3 = female pin header, 2 pins [form="♀ (female)"]
  CTRL4 = female pin header, 2 pins [form="♀ (female)"]
  CTRL5 = female pin header, 2 pins [form="♀ (female)"]
  CTRL6 = female pin header, 2 pins [form="♀ (female)"]
  CTRL7 = female pin header, 2 pins [form="♀ (female)"]
  VDD_8V = female pin header, 2 pins [form="♀ (female)"]
  CTRL8 = female pin header, 2 pins [form="♀ (female)"]
  VDD_5V = female pin header, 2 pins [form="♀ (female)"]

nets (from the schematic view):
  N1: IC1.Y1#0, OUT1.pin2
  N2: IC1.AY2, IC6.AY2, CTRL6.pin1
  N3: IC1.RESET, CTRL8.pin2
  N4: IC1.AX3, IC6.AX3, CTRL4.pin2
  N5: IC1.AX0, IC6.AX0, CTRL3.pin1
  N6: IC1.X14, IC4.22, IC6.X14
  N7: IC1.X15, IC4.4, IC6.X15
  N8: IC1.X6, IC4.18, IC6.X6
  N9: IC1.X7, IC4.8, IC6.X7
  N10: IC1.X8, IC5.22, IC6.X8
  N11: IC1.X9, IC1.X1, IC2.4, IC5.4, IC6.X9, IC6.X1
  N12: IC1.X10, IC1.X2, IC2.18, IC5.18, IC6.X10, IC6.X2
  N13: IC1.X11, IC5.8, IC6.X11
  N14: IC1.Y7, OUT3.pin2
  N15: IC1.Y6, OUT3.pin1
  N16: IC1.STROBE, CTRL8.pin1
  N17: IC1.Y5, OUT2.pin2
  N18: IC1.VEE, IC6.VEE, VDD_8V.pin2
  N19: IC1.Y4, OUT2.pin1
  N20: IC1.AX1, IC6.AX1, CTRL3.pin2
  N21: IC1.AX2, IC6.AX2, CTRL4.pin1
  N22: IC1.AY0, IC6.AY0, CTRL5.pin1
  N23: IC1.AY1, IC6.AY1, CTRL5.pin2
  N24: IC1.X13, IC3.8, IC6.X13
  N25: IC1.X12, IC3.18, IC6.X12
  N26: IC1.X5, IC3.4, IC6.X5
  N27: IC1.X4, IC3.22, IC6.X4
  N28: IC1.X3, IC2.8, IC6.X3
  N29: IC1.X0, IC2.22, IC6.X0
  N30: IC1.Y0, OUT0.pin1
  N31: IC1.CS, CTRL7.pin2
  N32: IC1.Y1#36, OUT0.pin2
  N33: IC1.DATA, CTRL7.pin1
  N34: IC1.Y2, OUT1.pin1
  VDD: IC1.VDD, IC6.VDD, VDD_8V.pin1
  GND: IC2.1, IC2.5, IC2.17, IC2.21, IC3.1, IC3.5, IC3.17, IC3.21, IC5.1, IC5.5, IC5.17, IC5.21, IC4.1, IC4.5, IC4.17, IC4.21
  N35: IC2.3, IN0.pin1
  N36: IC2.7, IN0.pin2
  N37: IC2.9, IC3.9, IC5.9, IC4.9, VDD_5V.pin2
  N38: IC2.15, IC2.16, IC3.15, IC3.16, IC5.15, IC5.16, IC4.15, IC4.16, VDD_5V.pin1
  N39: IC2.19, IN1.pin2
  N40: IC2.23, IN1.pin1
  N41: IC3.3, IN2.pin1
  N42: IC3.7, IN2.pin2
  N43: IC3.19, IN3.pin2
  N44: IC3.23, IN3.pin1
  N45: IC5.3, IN5.pin1
  N46: IC5.7, IN5.pin2
  N47: IC5.19, IN6.pin2
  N48: IC5.23, IN6.pin1
  N49: IC4.3, IN4.pin1
  N50: IC4.7, IN4.pin2
  N51: IC4.19, IN7.pin2
  N52: IC4.23, IN7.pin1
  N53: IC6.Y1#0, OUT5.pin2
  N54: IC6.RESET, CTRL1.pin2
  N55: IC6.Y7, OUT7.pin2
  N56: IC6.Y6, OUT7.pin1
  N57: IC6.STROBE, CTRL1.pin1
  N58: IC6.Y5, OUT6.pin2
  N59: IC6.Y4, OUT6.pin1
  N60: IC6.Y0, OUT4.pin1
  N61: IC6.CS, CTRL2.pin1
  N62: IC6.Y1#36, OUT4.pin2
  N63: IC6.DATA, CTRL2.pin2
  N64: IC6.Y2, OUT5.pin1

custom parts:
  CD22M3494: CD22M3494 from Intersil http://www.icbase.com/pdf/ITS/ITS14170701.pdf
  AD8403: http://www.analog.com/static/imported-files/data_sheets/AD8400_8402_8403.pdf
