# Fritzing sketch arduino_shield (saved by Fritzing 0.9.0b)
circuit board: 11.8191cm x 7.01448cm
breadboards: 1

parts:
  SWITCH_CTRL = double row female pin header, 16 pins [form="♀ (female)"]
  POT_CTRL = double row female pin header, 16 pins [form="♀ (female)"]
  TOP_SHIFT_REGISTER = MCP23017 I2C I/O Expander
  TOP = double row female pin header, 16 pins [form="♀ (female)"]
  BOTTOM = double row female pin header, 16 pins [form="♀ (female)"]
  R1 = Resistor [tolerance=±5% resistance=10k package=THT]
  R2 = Resistor [tolerance=±5% resistance=10k package=THT]
  R3 = Resistor [tolerance=±5% resistance=220 package=THT]
  R4 = Resistor [tolerance=±5% resistance=220 package=THT]
  R5 = Resistor [tolerance=±5% resistance=220 package=THT]
  R6 = Resistor [tolerance=±5% resistance=220 package=THT]
  R7 = Resistor [tolerance=±5% resistance=220 package=THT]
  R8 = Resistor [tolerance=±5% resistance=220 package=THT]
  R10 = Resistor [tolerance=±5% resistance=220 package=THT]
  R9 = Resistor [tolerance=±5% resistance=220 package=THT]
  R11 = Resistor [tolerance=±5% resistance=220 package=THT]
  R12 = Resistor [tolerance=±5% resistance=220 package=THT]
  R13 = Resistor [tolerance=±5% resistance=220 package=THT]
  R14 = Resistor [tolerance=±5% resistance=220 package=THT]
  R15 = Resistor [tolerance=±5% resistance=220 package=THT]
  R16 = Resistor [tolerance=±5% resistance=220 package=THT]
  R17 = Resistor [tolerance=±5% resistance=220 package=THT]
  R18 = Resistor [tolerance=±5% resistance=220 package=THT]
  R19 = Resistor [tolerance=±5% resistance=220 package=THT]
  R26 = Resistor [tolerance=±5% resistance=220 package=THT]
  R31 = Resistor [tolerance=±5% resistance=220 package=THT]
  R22 = Resistor [tolerance=±5% resistance=220 package=THT]
  R25 = Resistor [tolerance=±5% resistance=220 package=THT]
  R29 = Resistor [tolerance=±5% resistance=220 package=THT]
  R23 = Resistor [tolerance=±5% resistance=220 package=THT]
  R24 = Resistor [tolerance=±5% resistance=220 package=THT]
  R33 = Resistor [tolerance=±5% resistance=220 package=THT]
  R21 = Resistor [tolerance=±5% resistance=220 package=THT]
  R30 = Resistor [tolerance=±5% resistance=220 package=THT]
  R27 = Resistor [tolerance=±5% resistance=220 package=THT]
  R22_2 = Resistor [tolerance=±5% resistance=220 package=THT]
  R32 = Resistor [tolerance=±5% resistance=220 package=THT]
  R20 = Resistor [tolerance=±5% resistance=220 package=THT]
  R28 = Resistor [tolerance=±5% resistance=220 package=THT]
  BOTTOM_SHIFT_REGISTER = MCP23017 I2C I/O Expander
  I2C = female pin header, 2 pins [form="♀ (female)"]
  IC1 = 24LC128 [package=THT]
  IC2 = 24LC128 [package=THT]
  IC3 = 24LC128 [package=THT]
  IC4 = 24LC128 [package=THT]
  C1 = Ceramic Capacitor [capacitance=100nF package="100 mil [THT, multilayer]"]
  C2 = Ceramic Capacitor [capacitance=100nF package="100 mil [THT, multilayer]"]
  J2 = female pin header, 8 pins [form="♀ (female)"]  # not connected
  J3 = female pin header, 8 pins [form="♀ (female)"]  # not connected
  SPI = double row female pin header, 36 pins [form="♀ (female)"]
  J4 = female pin header, 8 pins [form="♀ (female)"]  # not connected
  I2C_2 = female pin header, 8 pins [form="♀ (female)"]
  J7 = female pin header, 10 pins [form="♀ (female)"]
  PDU = female pin header, 8 pins [form="♀ (female)"]

nets (from the pcb view):
  N1: SWITCH_CTRL.pin1, SPI.pin29
  N2: SWITCH_CTRL.pin2, SPI.pin28
  N3: SWITCH_CTRL.pin3, SPI.pin27
  N4: SWITCH_CTRL.pin4, SPI.pin26
  N5: SWITCH_CTRL.pin5, SPI.pin25
  N6: SWITCH_CTRL.pin6, SPI.pin24
  N7: SWITCH_CTRL.pin7, SPI.pin23
  N8: SWITCH_CTRL.pin8, SPI.pin22
  N9: SWITCH_CTRL.pin9, SPI.pin19
  N10: SWITCH_CTRL.pin10, POT_CTRL.pin10, SPI.pin36
  N11: SWITCH_CTRL.pin11, SPI.pin13
  N12: SWITCH_CTRL.pin12, SPI.pin12
  N13: SWITCH_CTRL.pin13, SPI.pin11
  N14: SWITCH_CTRL.pin14, SPI.pin10
  N15: SWITCH_CTRL.pin15, SPI.pin9
  VSS: SWITCH_CTRL.pin16, TOP_SHIFT_REGISTER.VSS, TOP_SHIFT_REGISTER.SCL, TOP_SHIFT_REGISTER.A0, TOP_SHIFT_REGISTER.A1, TOP_SHIFT_REGISTER.A2, BOTTOM_SHIFT_REGISTER.VSS, BOTTOM_SHIFT_REGISTER.SCL, BOTTOM_SHIFT_REGISTER.A1, BOTTOM_SHIFT_REGISTER.A2, I2C.pin2, IC1.A1, IC1.A2, IC1.0V, IC1.SCL_-_I2C_Clock, IC2.A2, IC2.0V, IC2.SCL_-_I2C_Clock, IC3.0V, IC3.SCL_-_I2C_Clock, IC4.A1, IC4.0V, IC4.SCL_-_I2C_Clock, I2C_2.pin1, J7.pin7, PDU.pin2, PDU.pin3
  N16: POT_CTRL.pin1, SPI.pin3
  N17: POT_CTRL.pin2, SPI.pin5
  N18: POT_CTRL.pin3, SPI.pin32
  N19: POT_CTRL.pin4, SPI.pin7
  N20: POT_CTRL.pin5, SPI.pin30
  N21: POT_CTRL.pin9, R2.Pin_1, BOTTOM_SHIFT_REGISTER.VDD, BOTTOM_SHIFT_REGISTER.A0, C1.0, C1.1, C2.1, PDU.pin4
  N22: POT_CTRL.pin12, SPI.pin31
  N23: POT_CTRL.pin13, SPI.pin6
  N24: POT_CTRL.pin14, SPI.pin33
  N25: POT_CTRL.pin15, SPI.pin4
  N26: POT_CTRL.pin16, SPI.pin35
  N27: TOP_SHIFT_REGISTER.GPB0, R11.Pin_1
  N28: TOP_SHIFT_REGISTER.GPB1, R12.Pin_1
  N29: TOP_SHIFT_REGISTER.GPB2, R13.Pin_1
  N30: TOP_SHIFT_REGISTER.GPB3, R14.Pin_1
  N31: TOP_SHIFT_REGISTER.GPB4, R15.Pin_1
  N32: TOP_SHIFT_REGISTER.GPB5, R16.Pin_1
  N33: TOP_SHIFT_REGISTER.GPB6, R17.Pin_1
  N34: TOP_SHIFT_REGISTER.GPB7, R18.Pin_1
  N35: TOP_SHIFT_REGISTER.VDD, R1.Pin_1, IC1.A0, IC1.WP_-_Write_Protect, IC1.+V, IC2.A0, IC2.A1, IC2.WP_-_Write_Protect, IC2.+V, IC3.A0, IC3.A1, IC3.A2, IC3.WP_-_Write_Protect, IC3.+V, IC4.A0, IC4.A2, IC4.WP_-_Write_Protect, IC4.+V, C2.0
  N36: TOP_SHIFT_REGISTER.SDA, BOTTOM_SHIFT_REGISTER.SDA, I2C.pin1, IC1.SDA_-_I2C_Data, IC2.SDA_-_I2C_Data, IC3.SDA_-_I2C_Data, IC4.SDA_-_I2C_Data, I2C_2.pin2
  N37: TOP_SHIFT_REGISTER.RESET, R1.Pin_0
  N38: TOP_SHIFT_REGISTER.GPA0, R3.Pin_1
  N39: TOP_SHIFT_REGISTER.GPA1, R4.Pin_1
  N40: TOP_SHIFT_REGISTER.GPA2, R5.Pin_1
  N41: TOP_SHIFT_REGISTER.GPA3, R6.Pin_1
  N42: TOP_SHIFT_REGISTER.GPA4, R7.Pin_1
  N43: TOP_SHIFT_REGISTER.GPA5, R8.Pin_1
  N44: TOP_SHIFT_REGISTER.GPA6, R9.Pin_1
  N45: TOP_SHIFT_REGISTER.GPA7, R10.Pin_1
  N46: TOP.pin1, R10.Pin_0
  N47: TOP.pin2, R9.Pin_0
  N48: TOP.pin3, R8.Pin_0
  N49: TOP.pin4, R7.Pin_0
  N50: TOP.pin5, R6.Pin_0
  N51: TOP.pin6, R5.Pin_0
  N52: TOP.pin7, R4.Pin_0
  N53: TOP.pin8, R3.Pin_0
  N54: TOP.pin9, R18.Pin_0
  N55: TOP.pin10, R17.Pin_0
  N56: TOP.pin11, R16.Pin_0
  N57: TOP.pin12, R15.Pin_0
  N58: TOP.pin13, R14.Pin_0
  N59: TOP.pin14, R13.Pin_0
  N60: TOP.pin15, R12.Pin_0
  N61: TOP.pin16, R11.Pin_0
  N62: BOTTOM.pin1, R25.Pin_0
  N63: BOTTOM.pin2, R24.Pin_0
  N64: BOTTOM.pin3, R23.Pin_0
  N65: BOTTOM.pin4, R22_2.Pin_0
  N66: BOTTOM.pin5, R22.Pin_0
  N67: BOTTOM.pin6, R21.Pin_0
  N68: BOTTOM.pin7, R20.Pin_0
  N69: BOTTOM.pin8, R19.Pin_0
  N70: BOTTOM.pin9, R33.Pin_0
  N71: BOTTOM.pin10, R32.Pin_0
  N72: BOTTOM.pin11, R31.Pin_0
  N73: BOTTOM.pin12, R30.Pin_0
  N74: BOTTOM.pin13, R29.Pin_0
  N75: BOTTOM.pin14, R28.Pin_0
  N76: BOTTOM.pin15, R27.Pin_0
  N77: BOTTOM.pin16, R26.Pin_0
  N78: R2.Pin_0, BOTTOM_SHIFT_REGISTER.RESET
  N79: R19.Pin_1, BOTTOM_SHIFT_REGISTER.GPA0
  N80: R26.Pin_1, BOTTOM_SHIFT_REGISTER.GPB0
  N81: R31.Pin_1, BOTTOM_SHIFT_REGISTER.GPB5
  N82: R22.Pin_1, BOTTOM_SHIFT_REGISTER.GPA3
  N83: R25.Pin_1, BOTTOM_SHIFT_REGISTER.GPA7
  N84: R29.Pin_1, BOTTOM_SHIFT_REGISTER.GPB3
  N85: R23.Pin_1, BOTTOM_SHIFT_REGISTER.GPA5
  N86: R24.Pin_1, BOTTOM_SHIFT_REGISTER.GPA6
  N87: R33.Pin_1, BOTTOM_SHIFT_REGISTER.GPB7
  N88: R21.Pin_1, BOTTOM_SHIFT_REGISTER.GPA2
  N89: R30.Pin_1, BOTTOM_SHIFT_REGISTER.GPB4
  N90: R27.Pin_1, BOTTOM_SHIFT_REGISTER.GPB1
  N91: R22_2.Pin_1, BOTTOM_SHIFT_REGISTER.GPA4
  N92: R32.Pin_1, BOTTOM_SHIFT_REGISTER.GPB6
  N93: R20.Pin_1, BOTTOM_SHIFT_REGISTER.GPA1
  N94: R28.Pin_1, BOTTOM_SHIFT_REGISTER.GPB2

notes:
  SDA
  SCL
  GND
  5V
  3V3
  Amnesia - Shield 1.0

custom parts:
  MCP23017 I2C I/O Expander: MCP23017 I2C 16-Channel I/O Expander
