# Fritzing sketch led_output_board (saved by Fritzing 0.9.0b)
circuit board: 10cm x 13cm
breadboards: 1

parts:
  U1 = 74HC595 [package="DIP16 [THT]"]
  R1 = Resistor [tolerance=±5% resistance=220 package=THT]
  R2 = Resistor [tolerance=±5% resistance=220 package=THT]
  R3 = Resistor [tolerance=±5% resistance=220 package=THT]
  R4 = Resistor [tolerance=±5% resistance=220 package=THT]
  R5 = Resistor [tolerance=±5% resistance=220 package=THT]
  R6 = Resistor [tolerance=±5% resistance=220 package=THT]
  R7 = Resistor [tolerance=±5% resistance=220 package=THT]
  R8 = Resistor [tolerance=±5% resistance=220 package=THT]
  R9 = Resistor [tolerance=±5% resistance=220 package=THT]
  R10 = Resistor [tolerance=±5% resistance=220 package=THT]
  R11 = Resistor [tolerance=±5% resistance=220 package=THT]
  R12 = Resistor [tolerance=±5% resistance=220 package=THT]
  R13 = Resistor [tolerance=±5% resistance=220 package=THT]
  R14 = Resistor [tolerance=±5% resistance=220 package=THT]
  R15 = Resistor [tolerance=±5% resistance=220 package=THT]
  R16 = Resistor [tolerance=±5% resistance=220 package=THT]
  U3 = 74HC595 [package="DIP16 [THT]"]
  U4 = 74HC595 [package="DIP16 [THT]"]
  U5 = 74HC595 [package="DIP16 [THT]"]
  U6 = 74HC595 [package="DIP16 [THT]"]
  J2 = shrouded pin header, 16 pins [form="♂ (shrouded male)"]
  R17 = Resistor [tolerance=±5% resistance=220 package=THT]
  R18 = Resistor [tolerance=±5% resistance=220 package=THT]
  R19 = Resistor [tolerance=±5% resistance=220 package=THT]
  R20 = Resistor [tolerance=±5% resistance=220 package=THT]
  R21 = Resistor [tolerance=±5% resistance=220 package=THT]
  R22 = Resistor [tolerance=±5% resistance=220 package=THT]
  R23 = Resistor [tolerance=±5% resistance=220 package=THT]
  R24 = Resistor [tolerance=±5% resistance=220 package=THT]
  R25 = Resistor [tolerance=±5% resistance=220 package=THT]
  R26 = Resistor [tolerance=±5% resistance=220 package=THT]
  R28 = Resistor [tolerance=±5% resistance=220 package=THT]
  R29 = Resistor [tolerance=±5% resistance=220 package=THT]
  R30 = Resistor [tolerance=±5% resistance=220 package=THT]
  R31 = Resistor [tolerance=±5% resistance=220 package=THT]
  R32 = Resistor [tolerance=±5% resistance=220 package=THT]
  J3 = shrouded pin header, 16 pins [form="♂ (shrouded male)"]
  R33 = Resistor [tolerance=±5% resistance=220 package=THT]
  R34 = Resistor [tolerance=±5% resistance=220 package=THT]
  R35 = Resistor [tolerance=±5% resistance=220 package=THT]
  R36 = Resistor [tolerance=±5% resistance=220 package=THT]
  R37 = Resistor [tolerance=±5% resistance=220 package=THT]
  R38 = Resistor [tolerance=±5% resistance=220 package=THT]
  R39 = Resistor [tolerance=±5% resistance=220 package=THT]
  R40 = Resistor [tolerance=±5% resistance=220 package=THT]
  R41 = Resistor [tolerance=±5% resistance=220 package=THT]
  R42 = Resistor [tolerance=±5% resistance=220 package=THT]
  R43 = Resistor [tolerance=±5% resistance=220 package=THT]
  R44 = Resistor [tolerance=±5% resistance=220 package=THT]
  R45 = Resistor [tolerance=±5% resistance=220 package=THT]
  R46 = Resistor [tolerance=±5% resistance=220 package=THT]
  R47 = Resistor [tolerance=±5% resistance=220 package=THT]
  R48 = Resistor [tolerance=±5% resistance=220 package=THT]
  J4 = shrouded pin header, 16 pins [form="♂ (shrouded male)"]
  C1 = Tantalum Capacitor [capacitance=1μF package="100 mil [THT, tantalum]"]
  C2 = Tantalum Capacitor [capacitance=1μF package="100 mil [THT, tantalum]"]
  C3 = Tantalum Capacitor [capacitance=1μF package="100 mil [THT, tantalum]"]
  U2 = 74HC595 [package="DIP16 [THT]"]
  R49 = Resistor [tolerance=±5% resistance=220 package=THT]
  J7 = female pin header, 1 pin [form="♀ (female)"]  # not connected
  J1 = shrouded pin header, 10 pins [form="♂ (shrouded male)"]  # not connected
  J11 = female pin header, 5 pins [form="♀ (female)"]
  J12 = female pin header, 5 pins [form="♀ (female)"]
  J13 = female pin header, 1 pin [form="♀ (female)"]  # not connected
  J14 = female pin header, 1 pin [form="♀ (female)"]  # not connected
  J15 = female pin header, 1 pin [form="♀ (female)"]  # not connected
  J16 = female pin header, 1 pin [form="♀ (female)"]  # not connected
  J17 = female pin header, 1 pin [form="♀ (female)"]  # not connected
  J18 = female pin header, 1 pin [form="♀ (female)"]  # not connected
  J19 = female pin header, 5 pins [form="♀ (female)"]
  J20 = female pin header, 5 pins [form="♀ (female)"]
  J21 = female pin header, 1 pin [form="♀ (female)"]
  J22 = female pin header, 1 pin [form="♀ (female)"]
  J23 = female pin header, 1 pin [form="♀ (female)"]
  J24 = female pin header, 1 pin [form="♀ (female)"]
  J25 = female pin header, 1 pin [form="♀ (female)"]
  J26 = female pin header, 1 pin [form="♀ (female)"]
  C4 = Tantalum Capacitor [capacitance=1μF package="100 mil [THT, tantalum]"]
  C5 = Tantalum Capacitor [capacitance=1μF package="100 mil [THT, tantalum]"]
  C6 = Tantalum Capacitor [capacitance=1μF package="100 mil [THT, tantalum]"]
  J27 = female pin header, 1 pin [form="♀ (female)"]
  J28 = female pin header, 1 pin [form="♀ (female)"]
  J29 = female pin header, 1 pin [form="♀ (female)"]
  J30 = female pin header, 1 pin [form="♀ (female)"]
  J31 = female pin header, 1 pin [form="♀ (female)"]
  J32 = female pin header, 1 pin [form="♀ (female)"]
  J34 = female pin header, 1 pin [form="♀ (female)"]
  J37 = female pin header, 1 pin [form="♀ (female)"]
  J38 = female pin header, 1 pin [form="♀ (female)"]

nets:
  N1: U1.Q1, R2.Pin_1
  N2: U1.Q2, R3.Pin_1
  N3: U1.Q3, R4.Pin_1
  N4: U1.Q4, R5.Pin_1
  N5: U1.Q5, R6.Pin_1
  N6: U1.Q6, R7.Pin_1
  N7: U1.Q7, R8.Pin_1
  N8: U1.Q7', U2.DS
  VCC: U1.MR, U1.VCC, U3.MR, U3.VCC, U5.MR, U5.VCC
  N9: U1.ST_CP, C3.+
  N10: U1.OE, U3.OE, U5.OE
  N11: U1.Q0, R1.Pin_1
  N12: R1.Pin_0, J2.pin16
  N13: R2.Pin_0, J2.pin15
  N14: R3.Pin_0, J2.pin14
  N15: R4.Pin_0, J2.pin13
  N16: R5.Pin_0, J2.pin12
  N17: R6.Pin_0, J2.pin11
  N18: R7.Pin_0, J2.pin10
  N19: R8.Pin_0, J2.pin9
  N20: R9.Pin_0, J2.pin8
  N21: R9.Pin_1, U2.Q0
  N22: R10.Pin_0, J2.pin7
  N23: R10.Pin_1, U2.Q1
  N24: R11.Pin_0, J2.pin6
  N25: R11.Pin_1, U2.Q2
  N26: R12.Pin_0, J2.pin5
  N27: R12.Pin_1, U2.Q3
  N28: R13.Pin_0, J2.pin4
  N29: R13.Pin_1, U2.Q4
  N30: R14.Pin_0, J2.pin3
  N31: R14.Pin_1, U2.Q5
  N32: R15.Pin_0, J2.pin2
  N33: R15.Pin_1, U2.Q6
  N34: R16.Pin_0, J2.pin1
  N35: R16.Pin_1, U2.Q7
  N36: U3.Q1, R24.Pin_1
  N37: U3.Q2, R29.Pin_1
  N38: U3.Q3, R25.Pin_1
  N39: U3.Q4, R18.Pin_1
  N40: U3.Q5, R28.Pin_1
  N41: U3.Q6, R22.Pin_1
  N42: U3.Q7, R26.Pin_1
  N43: U3.ST_CP, C2.+
  N44: U3.Q0, R49.Pin_1
  N45: U4.Q1, R19.Pin_1
  N46: U4.Q2, R32.Pin_1
  N47: U4.Q3, R31.Pin_1
  N48: U4.Q4, R30.Pin_1
  N49: U4.Q5, R17.Pin_1
  N50: U4.Q6, R20.Pin_1
  N51: U4.Q7, R23.Pin_1
  GND: U4.GND, U6.GND
  N52: U4.Q7', U6.DS
  VCC_2: U4.MR, U4.VCC, U6.MR, U6.VCC, U2.MR, U2.VCC
  N53: U4.ST_CP, C5.+
  N54: U4.OE, U6.OE, U2.OE
  N55: U4.DS, U2.Q7'
  N56: U4.Q0, R21.Pin_1
  N57: U5.Q1, R40.Pin_1
  N58: U5.Q2, R45.Pin_1
  N59: U5.Q3, R41.Pin_1
  N60: U5.Q4, R34.Pin_1
  N61: U5.Q5, R44.Pin_1
  N62: U5.Q6, R38.Pin_1
  N63: U5.Q7, R42.Pin_1
  N64: U5.ST_CP, C1.+
  N65: U5.DS, U6.Q7'
  N66: U5.Q0, R43.Pin_1
  N67: U6.Q1, R39.Pin_1
  N68: U6.Q2, R48.Pin_1
  N69: U6.Q3, R47.Pin_1
  N70: U6.Q4, R46.Pin_1
  N71: U6.Q5, R33.Pin_1
  N72: U6.Q6, R36.Pin_1
  N73: U6.Q7, R35.Pin_1
  N74: U6.ST_CP, C6.+
  N75: U6.Q0, R37.Pin_1
  N76: R17.Pin_0, J3.pin3
  N77: R18.Pin_0, J3.pin12
  N78: R19.Pin_0, J3.pin7
  N79: R20.Pin_0, J3.pin2
  N80: R21.Pin_0, J3.pin8
  N81: R22.Pin_0, J3.pin10
  N82: R23.Pin_0, J3.pin1
  N83: R24.Pin_0, J3.pin15
  N84: R25.Pin_0, J3.pin13
  N85: R26.Pin_0, J3.pin9
  N86: R28.Pin_0, J3.pin11
  N87: R29.Pin_0, J3.pin14
  N88: R30.Pin_0, J3.pin4
  N89: R31.Pin_0, J3.pin5
  N90: R32.Pin_0, J3.pin6
  N91: J3.pin16, R49.Pin_0
  N92: R33.Pin_0, J4.pin3
  N93: R34.Pin_0, J4.pin12
  N94: R35.Pin_0, J4.pin1
  N95: R36.Pin_0, J4.pin2
  N96: R37.Pin_0, J4.pin8
  N97: R38.Pin_0, J4.pin10
  N98: R39.Pin_0, J4.pin7
  N99: R40.Pin_0, J4.pin15
  N100: R41.Pin_0, J4.pin13
  N101: R42.Pin_0, J4.pin9
  N102: R43.Pin_0, J4.pin16
  N103: R44.Pin_0, J4.pin11
  N104: R45.Pin_0, J4.pin14
  N105: R46.Pin_0, J4.pin4
  N106: R47.Pin_0, J4.pin5
  N107: R48.Pin_0, J4.pin6
  N108: U2.ST_CP, C4.+
  N109: J11.pin1, J12.pin1, J19.pin5, J20.pin5, J22.pin1, J24.pin1, J25.pin1
  N110: J11.pin2, J12.pin2, J19.pin4, J20.pin4, J21.pin1, J23.pin1, J26.pin1
  N111: J11.pin5, J30.pin1, J38.pin1
  N112: J12.pin5, J19.pin1, J20.pin1, J27.pin1, J28.pin1, J29.pin1
  N113: J31.pin1, J37.pin1
  N114: J32.pin1, J34.pin1
