# Fritzing sketch top_control_board (saved by Fritzing 0.8.7b)
circuit board: 28cm x 8cm
breadboards: 1

parts:
  S1 = Momentary Switch [package=ksa_sealed_tac_switch]
  S3 = Momentary Switch [package=ksa_sealed_tac_switch]
  S2 = Momentary Switch [package=ksa_sealed_tac_switch]
  S5 = Momentary Switch [package=ksa_sealed_tac_switch]
  S6 = Momentary Switch [package=ksa_sealed_tac_switch]
  S7 = Momentary Switch [package=ksa_sealed_tac_switch]
  S8 = Momentary Switch [package=ksa_sealed_tac_switch]
  S9 = Momentary Switch [package=ksa_sealed_tac_switch]
  S10 = Momentary Switch [package=ksa_sealed_tac_switch]
  S11 = Momentary Switch [package=ksa_sealed_tac_switch]
  S12 = Momentary Switch [package=ksa_sealed_tac_switch]
  S13 = Momentary Switch [package=ksa_sealed_tac_switch]
  S14 = Momentary Switch [package=ksa_sealed_tac_switch]
  S15 = Momentary Switch [package=ksa_sealed_tac_switch]
  S16 = Momentary Switch [package=ksa_sealed_tac_switch]
  S4 = Momentary Switch [package=ksa_sealed_tac_switch]
  U1 = 74HC595 [package="DIP16 [THT]"]
  U2 = 74HC595 [package="DIP16 [THT]"]
  LED1 = LED - 5mm [color="Red (633nm)" package="5 mm [THT]"]
  LED2 = LED - 5mm [color="Red (633nm)" package="5 mm [THT]"]
  LED3 = LED - 5mm [color="Red (633nm)" package="5 mm [THT]"]
  LED4 = LED - 5mm [color="Red (633nm)" package="5 mm [THT]"]
  LED5 = LED - 5mm [color="Red (633nm)" package="5 mm [THT]"]
  LED6 = LED - 5mm [color="Red (633nm)" package="5 mm [THT]"]
  LED7 = LED - 5mm [color="Red (633nm)" package="5 mm [THT]"]
  LED8 = LED - 5mm [color="Red (633nm)" package="5 mm [THT]"]
  LED9 = LED - 5mm [color="Red (633nm)" package="5 mm [THT]"]
  LED10 = LED - 5mm [color="Red (633nm)" package="5 mm [THT]"]
  LED11 = LED - 5mm [color="Red (633nm)" package="5 mm [THT]"]
  LED12 = LED - 5mm [color="Red (633nm)" package="5 mm [THT]"]
  LED13 = LED - 5mm [color="Red (633nm)" package="5 mm [THT]"]
  LED14 = LED - 5mm [color="Red (633nm)" package="5 mm [THT]"]
  LED15 = LED - 5mm [color="Red (633nm)" package="5 mm [THT]"]
  LED16 = LED - 5mm [color="Red (633nm)" package="5 mm [THT]"]
  RE1 = Rotary Encoder [package=THT]  # not connected

nets:
  GND: S1.2, S2.1
  N1: S3.1, S2.2
  N2: S3.2, S4.1
  N3: S5.1, S4.2
  N4: S5.2, S6.1
  N5: S6.2, S7.1
  N6: S7.2, S8.1
  N7: S8.2, S9.1
  N8: S9.2, S10.1
  N9: S10.2, S11.1
  N10: S11.2, S12.1
  N11: S12.2, S13.1
  N12: S13.2, S14.1
  N13: S14.2, S15.1
  N14: S15.2, S16.1
  N15: U1.Q1, LED2.anode
  N16: U1.Q2, LED3.anode
  N17: U1.Q3, LED4.anode
  N18: U1.Q4, LED5.anode
  N19: U1.Q5, LED6.anode
  N20: U1.Q6, LED7.anode
  N21: U1.Q7, LED8.anode
  N22: U1.Q7', U2.DS
  N23: U1.Q0, LED1.anode
  N24: U2.Q1, LED10.anode
  N25: U2.Q2, LED11.anode
  N26: U2.Q3, LED12.anode
  N27: U2.Q4, LED13.anode
  N28: U2.Q5, LED14.anode
  N29: U2.Q6, LED15.anode
  N30: U2.Q7, LED16.anode
  N31: U2.Q0, LED9.anode
